# Fritzing sketch Estampadora (saved by Fritzing 0.9.3b)
stripboards: 2
breadboards: 1

parts:
  Part1 = Arduino Nano (Rev3.0)
  LCD1 = LCD screen
  T1 = LM35 Temperature Sensor [package="TO92 [THT]"]
  8_Channel_Relay1 = richardbruneau00
  R3 = Rotary Potentiometer (Small) [maximum_resistance=100kΩ package=THT]
  VALVE1 = Plastic Solenoid Valve
  VALVE2 = Plastic Solenoid Valve
  VALVE3 = Plastic Solenoid Valve
  Power_plug1 = Power plug

nets:
  GND: Part1.GND, LCD1.VSS, LCD1.R/W, LCD1.LED-, T1.GND, 8_Channel_Relay1.connector8, R3.leg2
  N1: Part1.D4, LCD1.DB7
  N2: Part1.D5, LCD1.DB6
  N3: Part1.D6, LCD1.DB5
  N4: Part1.D7, LCD1.DB4
  N5: Part1.D8, LCD1.E
  N6: Part1.D9, LCD1.RS
  N7: Part1.D10, 8_Channel_Relay1.connector11
  N8: Part1.D11/MOSI, 8_Channel_Relay1.connector10
  N9: Part1.D12/MISO, 8_Channel_Relay1.connector9
  5V: Part1.5V, LCD1.VDD, LCD1.LED+, T1.+Vs, 8_Channel_Relay1.connector16, 8_Channel_Relay1.connector17, R3.leg1
  N10: Part1.A0, T1.Vout
  N11: LCD1.V0, R3.wiper
  N12: 8_Channel_Relay1.connector19, 8_Channel_Relay1.connector20
  N13: 8_Channel_Relay1.connector22, 8_Channel_Relay1.connector25, 8_Channel_Relay1.connector28, Power_plug1.GND
  N14: 8_Channel_Relay1.connector23, VALVE1.no_name_yet#2
  N15: 8_Channel_Relay1.connector26, VALVE2.no_name_yet#2
  N16: 8_Channel_Relay1.connector29, VALVE3.no_name_yet#2
  N17: VALVE1.no_name_yet#1, VALVE2.no_name_yet#1, VALVE3.no_name_yet#1, Power_plug1.VCC

notes:
  FALTA:
  Cambiar pantalla a I2C
  botones
  Sensores
